# Fritzing sketch demo circuit (saved by Fritzing 0.9.2b)
breadboards: 1

parts:
  Raspberry_Pi1 = Raspberry Pi 2
  LED1 = smd LED [color="Red (633nm)" package="0805 [SMD]"]
  LED2 = smd LED [color="Red (633nm)" package="0805 [SMD]"]
  LED3 = smd LED [color="Red (633nm)" package="0805 [SMD]"]
  LED4 = smd LED [color="Red (633nm)" package="0805 [SMD]"]
  R1 = Resistor [tolerance=±5% resistance=4.7k package="2010 [SMD]"]
  R2 = Resistor [tolerance=±5% resistance=4.7k package=THT]
  R3 = Resistor [tolerance=±5% resistance=4.7k package=THT]
  R4 = Resistor [tolerance=±5% resistance=4.7k package=THT]

nets:
  3V3: Raspberry_Pi1.3v3, Raspberry_Pi1.5V, R1.Pin_1, R2.Pin_1, R3.Pin_1, R4.Pin_1
  N1: Raspberry_Pi1.GPIO26, LED2.cathode
  N2: Raspberry_Pi1.GND, LED1.cathode
  N3: Raspberry_Pi1.GPIO21, LED4.cathode
  N4: Raspberry_Pi1.GPIO20, LED3.cathode
  N5: LED1.anode, R1.Pin_0
  N6: LED2.anode, R2.Pin_0
  N7: LED3.anode, R3.Pin_0
  N8: LED4.anode, R4.Pin_0

notes:
  LEDs are connected to GPIO 26, 20 and 21
  3.3 V power
  GND
